# Fritzing sketch wallswitch (saved by Fritzing 0.9.3b)

parts:
  U1 = ESP32-38PinWide [part_number=ESP32-38PinWide]
  LED1 = Super Flux RGB LED (com. cathode)
  LED2 = Super Flux RGB LED (com. anode)
  LED3 = Super Flux RGB LED (com. anode)
  LED4 = Super Flux RGB LED (com. anode)
  TTP223B2 = TTP223B Capacitive Touch Sensor Module
  TTP223B3 = TTP223B Capacitive Touch Sensor Module
  TTP223B4 = TTP223B Capacitive Touch Sensor Module
  U2 = Vibration Motor- ROB-08449 [package=vibe-motor-10mm]
  TTP223B1 = TTP223B Capacitive Touch Sensor Module
  DS1 = DS18B20 1-Wire Temperature Sensor [part_number=DS18B20]
  R1 = Resistor [tolerance=±5% resistance=4.7k package="0402 [SMD]"]

nets:
  VCC: U1.3.3, TTP223B2.VCC, TTP223B3.VCC, TTP223B4.VCC, TTP223B1.VCC
  N1: U1.GPIO35, TTP223B1.SIG
  N2: U1.GPIO32, LED2.blue_cathode
  N3: U1.GPIO33, LED2.green_cathode
  N4: U1.GPIO25, LED2.red_cathode
  N5: U1.GPIO26, DS1.DQ, R1.Pin_0
  N6: U1.GPIO27, LED4.blue_cathode
  N7: U1.GPIO14, LED4.green_cathode
  N8: U1.GPIO12, LED4.red_cathode
  GND: U1.GND, LED1.common_cathode, LED2.common_anode, LED3.common_anode, LED4.common_anode, TTP223B2.GND, TTP223B3.GND, TTP223B4.GND, U2.+, TTP223B1.GND
  N9: U1.GPIO13, TTP223B3.SIG
  N10: U1.GPIO15, TTP223B2.SIG
  N11: U1.GPIO2, LED3.blue_cathode
  N12: U1.GPIO4, LED3.red_cathode
  N13: U1.GPIO16, LED3.green_cathode
  N14: U1.GPIO17, LED1.blue_anode
  N15: U1.GPIO5, LED1.green_anode
  N16: U1.GPIO18, LED1.red_anode
  N17: U1.GPIO19, TTP223B4.SIG
  N18: U1.GPIO23, U2.-
  N19: DS1.GND, R1.Pin_1

custom parts:
  ESP32-38PinWide: Generic 38-Pin ESP32 with wide format (only access to one side of pins on a breadboard) based on Stephen Lilley's HiLetgo ESP-WROOM-32 ESP32 ESP-32S Development Board.
  TTP223B Capacitive Touch Sensor Module: The TTP223B capacitive touch sensor module uses the TTP223B IC. The appropriate voltage is approximately 2 to 5.5 volts.
